# Fritzing sketch SchaltungApparillo6 (saved by Fritzing 0.9.2b)
breadboards: 1

parts:
  Raspberry_Pi = Raspberry Pi 2
  FireLasersLED = LED - 5mm [color="Blue (470nm)" package="5 mm [THT]"]
  RotaryEncoder = ENCODER_RGB_CA [package=encoder_led_3]
  FireLasersBTN = Round Pushbutton
  UVLORelay_5V = RELAY [package=relay-g5q]
  BC548B = NPN-Transistor [package="SOT-23 [SMD]"]
  FireMissilesLED1 = LED - 5mm [color="Green (565nm)" package="5 mm [THT]"]
  BC548B_2 = NPN-Transistor [package="SOT-23 [SMD]"]
  LCDRelay_5V = RELAY [package=relay-g5q]
  R1 = Resistor [tolerance=±5% resistance=1.5k package=THT]
  R2 = Resistor [tolerance=±5% resistance=1.5k package=THT]
  LiPo1 = LIPO-2000mAh [package=lipo-2000]
  U1 = mystery part, 6 pins [chip_label=?]
  FireMissilesBTN = Round Pushbutton
  Justboom/Hifiberry = mystery part, 7 pins [chip_label=?]
  JBPowerSupply = mystery part, 2 pins [chip_label=?]
  D1 = Rectifier Diode [part_number=1N4001 package="300 mil [THT]"]
  D2 = Rectifier Diode [part_number=1N4001 package="300 mil [THT]"]

nets:
  3V3: Raspberry_Pi.3v3, Raspberry_Pi.3V3, RotaryEncoder.+, FireLasersBTN.leg1
  N1: Raspberry_Pi.GPIO2, Raspberry_Pi.GPIO3, Raspberry_Pi.GIPO19, Raspberry_Pi.GIPO18, Justboom/Hifiberry.pin1, Justboom/Hifiberry.pin2, Justboom/Hifiberry.pin5, Justboom/Hifiberry.pin6
  N2: Raspberry_Pi.GIPO17, RotaryEncoder.-B
  N3: Raspberry_Pi.GIPO27, RotaryEncoder.-G
  N4: Raspberry_Pi.GIPO22, RotaryEncoder.SW
  N5: Raspberry_Pi.GIPO9, R1.Pin_1
  N6: Raspberry_Pi.GIPO11, R2.Pin_1
  N7: Raspberry_Pi.GIPO21, Justboom/Hifiberry.pin3
  N8: Raspberry_Pi.GIPO20, Justboom/Hifiberry.pin4
  N9: Raspberry_Pi.GIPO7, FireLasersBTN.leg0
  N10: Raspberry_Pi.GIPO8, FireLasersLED.anode
  N11: Raspberry_Pi.GIPO24, RotaryEncoder.A
  N12: Raspberry_Pi.GIPO23, RotaryEncoder.B
  N13: Raspberry_Pi.GND, FireLasersLED.cathode, RotaryEncoder.C, UVLORelay_5V.COIL1, FireMissilesLED1.cathode, LCDRelay_5V.COIL1, LiPo1.-, U1.pin4
  N14: Raspberry_Pi.GIPO14, RotaryEncoder.-R
  N15: Raspberry_Pi.5V, BC548B.1, BC548B_2.1, JBPowerSupply.pin1
  N16: UVLORelay_5V.COIL2, BC548B.2
  N17: UVLORelay_5V.MAIN, LiPo1.+, FireMissilesBTN.leg1
  N18: UVLORelay_5V.NO, FireMissilesLED1.anode, U1.pin2, U1.pin3, FireMissilesBTN.leg0
  N19: BC548B.0, R1.Pin_0
  N20: BC548B_2.2, LCDRelay_5V.COIL2
  N21: BC548B_2.0, R2.Pin_0
  N22: U1.pin1, D2.anode
  N23: JBPowerSupply.pin2, D1.cathode
  N24: D1.anode, D2.cathode
